// Logisim project Basic_Gates.circ as structural Verilog: 1 circuit, main circuit main
module main (
  input  in_1,
  input  in_2,
  input  in_3,
  input  in_4,
  input  in_5,
  input  in_6,
  input  in_7,
  input  in_8,
  input  in_9,
  input  in_10,
  input  in_11,
  input  in_12,
  input  in_13,
  input  in_14,
  input  in_15,
  input  in_16,
  input  in_17,
  input  in_18,
  output out_19,
  output out_20,
  output out_21,
  output out_22,
  output out_23,
  output out_24,
  output out_25,
  output out_26,
  output out_27,
  output out_28
);

  and and_1 (out_20, in_3, in_4);
  and and_2 (out_23, in_8, in_9);
  and and_3 (out_25, in_12, in_13);
  and and_4 (out_27, in_16, in_17);
  or or_1 (out_21, in_1, in_5);
  or or_2 (out_24, in_7, in_10);
  or or_3 (out_26, in_11, in_14);
  or or_4 (out_28, in_15, in_18);
  not not_1 (out_19, in_2);
  not not_2 (out_22, in_6);

  // Notes on the sheet:
  //   AND GATE
  //   OR GATE
  //   NOT GATE
endmodule
