// Logisim project DE3.circ as structural Verilog: 1 circuit, main circuit main
module main (
  input  b3,
  input  g3,
  input  b2,
  input  g2,
  input  b1,
  input  bg,
  input  b0,
  input  g0,
  output g3_2,
  output b3_2,
  output g2_2,
  output b2_2,
  output g1,
  output b1_2,
  output g0_2,
  output b0_2
);

  xor xor_1 (g2_2, b3, b2);
  xor xor_2 (g1, b2, b1);
  xor xor_3 (g0_2, b1, b0);
  xor xor_4 (b2_2, g3, g2);
  xor xor_5 (b1_2, b2_2, bg);
  xor xor_6 (b0_2, b1_2, g0);

  assign b3_2 = g3;
  assign g3_2 = b3;

  // Notes on the sheet:
  //   BINARY TO GRAY
  //   GRAY TO BINARY
endmodule
