// Logisim project NAND_NOR_IMPLEMENTATION.circ as structural Verilog: 1 circuit, main circuit main
module main (
  input  in_1,
  input  in_2,
  input  in_3,
  input  in_4,
  input  in_5,
  input  in_6,
  input  in_7,
  input  in_8,
  output out_9,
  output out_10,
  output out_11,
  output out_12
);

  wire nand_1_out, nand_3_out, nand_4_out, nor_1_out, nor_2_out, nor_4_out;

  nand nand_1 (nand_1_out, in_1, in_3);
  nor nor_1 (nor_1_out, in_5, in_5);
  nor nor_2 (nor_2_out, in_7, in_7);
  nand nand_2 (out_9, nand_1_out, nand_1_out);
  nor nor_3 (out_11, nor_1_out, nor_2_out);
  nand nand_3 (nand_3_out, in_2, in_2);
  nand nand_4 (nand_4_out, in_4, in_4);
  nor nor_4 (nor_4_out, in_6, in_8);
  nand nand_5 (out_10, nand_3_out, nand_4_out);
  nor nor_5 (out_12, nor_4_out, nor_4_out);

  // Notes on the sheet:
  //   AND GATE USING NAND
  //   AND GATE USING NOR
  //   OR GATE USING NAND
  //   OR GATE USING NOR
endmodule
